# Fritzing sketch ArduinoSketch (saved by Fritzing 0.9.1b)
breadboards: 1

parts:
  Part1 = Arduino Uno (Rev3)
  Q1 = PNP-Transistor [package="TO92 [THT]"]
  IRLED1 = LED - 5mm [color="Infrared (940nm)" package="5 mm [THT]"]
  4_AA_-_6V = Battery

nets:
  N1: Part1.GND, IRLED1.cathode, 4_AA_-_6V.-
  N2: Part1.D3_PWM, Q1.B
  N3: Q1.E, 4_AA_-_6V.+
  N4: Q1.C, IRLED1.anode
