# Fritzing sketch ArduinoWiringLayout (saved by Fritzing 0.9.1b)
breadboards: 1

parts:
  Part1 = Arduino Uno (Rev3)
  Q1 = NPN-Transistor [package="TO92 [THT]"]
  VCC1 = 4 x AAA Battery Mount
  LED1 = LED - 5mm [color="Infrared (940nm)" package="5 mm [THT]"]
  LED2 = LED - 5mm [color="Infrared (940nm)" package="5 mm [THT]"]
  LED3 = LED - 5mm [color="Red (633nm)" package="5 mm [THT]"]
  GUMSTIX = shrouded pin header, 10 pins [form="♂ (shrouded male)"]

nets:
  N1: Part1.D8, GUMSTIX.pin5
  N2: Part1.D9_PWM, GUMSTIX.pin6
  N3: Part1.D10_PWM/SS, GUMSTIX.pin7
  N4: Part1.D11_PWM/MOSI, GUMSTIX.pin8
  N5: Part1.D12/MISO, GUMSTIX.pin9
  N6: Part1.D13/SCK, GUMSTIX.pin10
  N7: Part1.D3_PWM, Q1.B
  N8: Part1.D7, GUMSTIX.pin4
  N9: Part1.GND, VCC1.-, LED1.cathode, LED2.cathode, LED3.cathode
  N10: Q1.E, LED1.anode, LED2.anode, LED3.anode
  N11: Q1.C, VCC1.+
